// Logisim project Oblig2.circ as structural Verilog: 4 circuits, main circuit counter
module main (
);

  wire Clk_out, Decoder__8, Decoder__9, Decoder__10, Decoder__11, or_1_out, or_2_out, Reset_out, xor_1_out;
  wire [3:0] Counter_out;
  wire [7:0] controlled_buffer_1_out, R_q, ram_1_data, select_new_value;

  Clock Clk (.out(Clk_out));
  Button Reset (.out(Reset_out));
  counter Counter (.Clk(Clk_out), .Reset(Reset_out), .Out(Counter_out));
  RAM #(.addrWidth(4)) ram_1 (.addr(Counter_out), .data(ram_1_data), .sel(1'b1), .ld(1'b1), .clr(1'b0));  // open: clk
  decoder Decoder (.inp(ram_1_data[7:4]), ._8(Decoder__8), ._9(Decoder__9), ._10(Decoder__10), ._11(Decoder__11));
  select select (
    .Old_value(R_q), .Input(ram_1_data[3:0]), ._1___override_LSB__0___override_MSB(Decoder__8),
    .New_value(select_new_value));
  xor xor_1 (xor_1_out, Decoder__8, Decoder__9);
  assign controlled_buffer_1_out = xor_1_out ? select_new_value : 8'bz;  // Controlled_Buffer controlled_buffer_1
  or or_1 (or_1_out, xor_1_out, Decoder__10);
  RAM #(.addrWidth(4)) ram_2 (
    .addr(ram_1_data[3:0]), .data(controlled_buffer_1_out), .sel(or_2_out), .clk(Clk_out), .ld(Decoder__10),
    .clr(Reset_out));
  or or_2 (or_2_out, Decoder__10, Decoder__11);
  Register #(.trigger("falling")) R (
    .D(controlled_buffer_1_out), .en(or_1_out), .Q(R_q), .clk(Clk_out), .clr(Reset_out));
  assign controlled_buffer_1_out = Decoder__11 ? R_q : 8'bz;  // Controlled_Buffer controlled_buffer_2

  // Notes on the sheet:
  //   Instruksjonsminne
  //   Dataminne
endmodule

module counter (
  input  Clk,
  input  Reset,
  output [3:0] Out
);

  wire adder_1_cout, not_1_out;
  wire [3:0] adder_1_out;

  Register #(.width(4), .trigger("falling")) register_1 (
    .D(adder_1_out), .en(not_1_out), .Q(Out), .clk(Clk), .clr(Reset));
  Adder #(.width(4)) adder_1 (.a(Out), .b(4'b0001), .out(adder_1_out), .cin(1'b0), .cout(adder_1_cout));
  not not_1 (not_1_out, adder_1_cout);
endmodule

module decoder (
  input  [3:0] inp,
  output _8,
  output _9,
  output _10,
  output _11
);

  Decoder #(.select(4)) decoder_1 (
    .out8(_8), .out9(_9), .out10(_10), .out11(_11), .sel(inp));  // open: out0, out1, out2, out3, out4, out5, out6, out7, out12, out13, out14, out15, en
endmodule

module select (
  input  [7:0] Old_value,
  input  [3:0] Input,
  input  _1___override_LSB__0___override_MSB,
  output [7:0] New_value
);

  wire not_1_out;

  assign New_value[7:4] = _1___override_LSB__0___override_MSB ? Old_value[7:4] : 4'bz;  // Controlled_Buffer controlled_buffer_1
  assign New_value[3:0] = not_1_out ? Old_value[3:0] : 4'bz;  // Controlled_Buffer controlled_buffer_2
  assign New_value[3:0] = _1___override_LSB__0___override_MSB ? Input : 4'bz;  // Controlled_Buffer controlled_buffer_3
  assign New_value[7:4] = not_1_out ? Input : 4'bz;  // Controlled_Buffer controlled_buffer_4
  not not_1 (not_1_out, _1___override_LSB__0___override_MSB);
endmodule
